// Logisim project budget_cpu.circ as structural Verilog: 1 circuit, main circuit main
module main (
  output [3:0] out_1,
  output [7:0] out_2
);

  wire and_1_out, and_2_out, and_3_out, and_4_out, and_5_out, DataTimer_out, decoder_1_out0, decoder_1_out1,
       decoder_1_out2, decoder_1_out3, not_1_out, Timer_out;
  wire [7:0] adder_1_out, adder_2_out, multiplexer_1_out, multiplexer_2_out, multiplexer_3_out, ram_1_dout,
       ram_2_dout, register_1_q, subtractor_1_out, X0_q, X1_q, X2_q, X3_q;

  Adder adder_1 (.a(register_1_q), .b(8'h1), .out(adder_1_out));  // open: cin, cout
  Clock #(.highDuration(2), .lowDuration(2)) Timer (.out(Timer_out));
  Clock DataTimer (.out(DataTimer_out));
  Register register_1 (.D(adder_1_out), .clk(Timer_out), .Q(register_1_q));  // open: en, clr
  and and_1 (and_1_out, ram_2_dout[7], ram_2_dout[6]);
  RAM #(.addrWidth(4)) ram_1 (
    .addr(out_1), .we(and_1_out), .oe(1'b1), .clk(DataTimer_out), .dout(ram_1_dout));  // open: din
  RAM ram_2 (
    .addr(register_1_q), .we(1'b0), .oe(1'b1), .clk(Timer_out),
    .dout({ram_2_dout[7:6], out_1, ram_2_dout[1:0]}));  // open: din
  not not_1 (not_1_out, and_1_out);
  Multiplexer #(.width(8)) multiplexer_1 (.in0(out_2), .in1(ram_1_dout), .out(multiplexer_1_out), .sel(ram_2_dout[7]));
  Decoder #(.select(2)) decoder_1 (
    .out0(decoder_1_out0), .out1(decoder_1_out1), .out2(decoder_1_out2), .out3(decoder_1_out3),
    .sel(ram_2_dout[1:0]));  // open: en
  and and_2 (and_2_out, not_1_out, decoder_1_out0);
  and and_3 (and_3_out, not_1_out, decoder_1_out1);
  and and_4 (and_4_out, not_1_out, decoder_1_out2);
  and and_5 (and_5_out, not_1_out, decoder_1_out3);
  Register X0 (.D(multiplexer_1_out), .en(and_2_out), .clk(Timer_out), .Q(X0_q));  // open: clr
  Register X1 (.D(multiplexer_1_out), .en(and_3_out), .clk(Timer_out), .Q(X1_q));  // open: clr
  Register X2 (.D(multiplexer_1_out), .en(and_4_out), .clk(Timer_out), .Q(X2_q));  // open: clr
  Register X3 (.D(multiplexer_1_out), .en(and_5_out), .clk(Timer_out), .Q(X3_q));  // open: clr
  Multiplexer #(.select(2), .width(8)) multiplexer_2 (
    .in0(X0_q), .in1(X1_q), .in2(X2_q), .in3(X3_q), .out(multiplexer_2_out), .sel(out_1[1:0]));
  Multiplexer #(.select(2), .width(8)) multiplexer_3 (
    .in0(X0_q), .in1(X1_q), .in2(X2_q), .in3(X3_q), .out(multiplexer_3_out), .sel(out_1[3:2]));
  Adder adder_2 (.a(multiplexer_2_out), .b(multiplexer_3_out), .out(adder_2_out));  // open: cin, cout
  Subtractor subtractor_1 (.a(multiplexer_2_out), .b(multiplexer_3_out), .out(subtractor_1_out));  // open: bin, bout
  Multiplexer #(.width(8)) multiplexer_4 (.in0(adder_2_out), .in1(subtractor_1_out), .out(out_2), .sel(ram_2_dout[6]));

  // Notes on the sheet:
  //   Christian Apostol, Marcus San Antonio
  //   CPU Name: Budget CPU
  //   I pledge my honor that I have abided by the Stevens Honor System.
  //   Instruction Fetching (IF)
  //   Instruction Memory
  //   Data Memory
  //   Instruction Decoding (ID)
  //   Write Back (WB)
  //   DestinationReg
  //   Memory Access (ME)
  //   RegWrite
  //   ReadReg1
  //   ReadReg2
  //   RegData1
  //   RegData2
  //   imm4
  //   Execution (EX)
  //   ALU
endmodule
